// Logisim project LC-2200-16.circ as structural Verilog
module ALU (
  input  [15:0] A,
  input  [15:0] B,
  input  [1:0] func,
  input  DrALU,
  output [15:0] Output
);

  wire [15:0] adder_1_out, adder_2_out, nand_1_out, subtractor_1_out;

  Subtractor #(.width(16)) subtractor_1 (.a(A), .b(B), .out(subtractor_1_out));  // open: bin, bout
  assign nand_1_out = ~(A & B);  // NAND_Gate nand_1, 16 bits wide
  Adder #(.width(16)) adder_1 (.a(A), .b(B), .out(adder_1_out));  // open: cin, cout
  Adder #(.width(16)) adder_2 (.a(16'h1), .b(A), .out(adder_2_out));  // open: cin, cout
  Multiplexer #(.select(2), .width(16)) multiplexer_1 (
    .in0(adder_1_out), .in1(nand_1_out), .in2(subtractor_1_out), .in3(adder_2_out), .out(Output), .sel(func),
    .en(DrALU));
endmodule
